// Logisim project main.circ as structural Verilog: 1 circuit, main circuit main
module main (
  input  [3:0] A,
  input  [3:0] B,
  input  [1:0] Control,
  output [7:0] Output
);

  wire [1:0] rom_3_data_3;
  wire [3:0] A_out1, A_out2, adder_1_out, B_out1, B_out2, bit_extender_5_out, divider_1_out, divider_1_rem,
       multiplier_1_cout, multiplier_1_out, rom_3_data, rom_3_data_2, subtractor_1_out;
  wire [4:4] adder_1_cout, rom_1_data, rom_2_data, subtractor_1_bout;
  wire [7:0] bit_extender_3_out, bit_extender_4_out;

  Hex_Digit_Display hex_digit_display_1 (.value(A_out2));  // open: dp
  Hex_Digit_Display hex_digit_display_2 (.value(A_out1));  // open: dp
  Hex_Digit_Display hex_digit_display_3 (.value(B_out1));  // open: dp
  Hex_Digit_Display hex_digit_display_4 (.value(B_out2));  // open: dp
  ROM #(.addrWidth(4), .dataWidth(5)) rom_1 (.addr(A), .data({rom_1_data[4], A_out2}));  // open: sel
  ROM #(.addrWidth(4), .dataWidth(5)) rom_2 (.addr(B), .data({rom_2_data[4], B_out2}));  // open: sel
  Hex_Digit_Display hex_digit_display_5 (.value(bit_extender_5_out));  // open: dp
  Adder #(.width(4)) adder_1 (.a(A), .b(B), .out(adder_1_out), .cout(adder_1_cout[4]));  // open: cin
  Subtractor #(.width(4)) subtractor_1 (
    .a(A), .b(B), .out(subtractor_1_out), .bout(subtractor_1_bout[4]));  // open: bin
  Multiplier #(.width(4)) multiplier_1 (.a(A), .b(B), .out(multiplier_1_out), .cout(multiplier_1_cout));  // open: cin
  Divider #(.width(4)) divider_1 (.a(A), .b(B), .out(divider_1_out), .rem(divider_1_rem));  // open: upper
  assign A_out1 = {{3{1'b0}}, rom_1_data[4]};  // Bit_Extender bit_extender_1
  assign B_out1 = {{3{1'b0}}, rom_2_data[4]};  // Bit_Extender bit_extender_2
  Hex_Digit_Display hex_digit_display_6 (.value(rom_3_data));  // open: dp
  Hex_Digit_Display hex_digit_display_7 (.value(rom_3_data_2));  // open: dp
  assign bit_extender_3_out = {{3{1'b0}}, {adder_1_cout[4], adder_1_out}};  // Bit_Extender bit_extender_3
  assign bit_extender_4_out = {{3{1'b0}}, {subtractor_1_bout[4], subtractor_1_out}};  // Bit_Extender bit_extender_4
  Multiplexer #(.select(2), .width(8)) multiplexer_1 (
    .in0(bit_extender_3_out), .in1(bit_extender_4_out), .in2({multiplier_1_cout, multiplier_1_out}),
    .in3({divider_1_rem, divider_1_out}), .out(Output), .sel(Control));  // open: en
  assign bit_extender_5_out = {{2{1'b0}}, rom_3_data_3};  // Bit_Extender bit_extender_5
  ROM #(.dataWidth(10)) rom_3 (.addr(Output), .data({rom_3_data_3, rom_3_data_2, rom_3_data}));  // open: sel

  // Other names for the same wires on the sheet: A_in[3:0] = A; B_in[3:0] = B

  // Notes on the sheet:
  //   contents of rom_1 (hex, n*v repeats v):
  //   0 1 2 3 4 5 6 7 8 9 10 11 12 13 14 15
  //   contents of rom_2 (hex, n*v repeats v):
  //   0 1 2 3 4 5 6 7 8 9 10 11 12 13 14 15
  //   =
  //   S1 --- S0 --- Out
  //   0   ---  0   ---  + 
  //   0   ---  1  ---  - 
  //   1  --- 0  --- * 
  //   1  --- 1  --- /
  //   contents of rom_3 (hex, n*v repeats v):
  //   0 1 2 3 4 5 6 7 8 9 10 11 12 13 14 15 16 17 18 19 20 21 22 23 24 25 26 27 28 29 30 31 32 33 34 35 36
  //   37 38 39 40 41 42 43 44 45 46 47 48 49 50 51 52 53 54 55 56 57 58 59 60 61 62 63 64 65 66 67 68 69
  //   70 71 72 73 74 75 76 77 78 79 80 81 82 83 84 85 86 87 88 89 90 91 92 93 94 95 96 97 98 99 100 101
  //   102 103 104 105 106 107 108 109 110 111 112 113 114 115 116 117 118 119 120 121 122 123 124 125 126
  //   127 128 129 130 131 132 133 134 135 136 137 138 139 140 141 142 143 144 145 146 147 148 149 150 151
  //   152 153 154 155 156 157 158 159 160 161 162 163 164 165 166 167 168 169 170 171 172 173 174 175 176
  //   177 178 179 180 181 182 183 184 185 186 187 188 189 190 191 192 193 194 195 196 197 198 199 200 201
  //   202 203 204 205 206 207 208 209 210 211 212 213 214 215 216 217 218 219 220 221 222 223 224 225 226
  //   227 228 229 230 231 232 233 234 235 236 237 238 239 240 241 242 243 244 245 246 247 248 249 250 251
  //   252 253 254 255
endmodule
